# Fritzing sketch SB-Cap-Fritzing-PCB-v1-Yun (saved by Fritzing 0.9.2b)
circuit board: 6.88566cm x 5.36311cm
breadboards: 1

parts:
  J1 = Basic Force Sensing Resistor (FSR) [package=THT]
  R1 = Resistor [tolerance=±5% resistance=1k package=THT]
  S1 = Tilt Switch [package=THT]
  R2 = Resistor [tolerance=±5% resistance=1k package=THT]
  R3 = Resistor [tolerance=±5% resistance=1k package=THT]
  U1 = Vibration Motor- ROB-08449 [package=vibe-motor-10mm]
  Cap_Prototype_Sheild = Arduino Yun

nets:
  N1: J1.pin_0, R2.Pin_0, R3.Pin_1, U1.-, Cap_Prototype_Sheild.A1, Cap_Prototype_Sheild.5V
  N2: J1.pin_1, R1.Pin_0, Cap_Prototype_Sheild.A0
  N3: R1.Pin_1, S1.Pin_2, Cap_Prototype_Sheild.GND
  N4: S1.Pin_1, R2.Pin_1, Cap_Prototype_Sheild.D2

// code stored in the sketch: SB-Cap-Fritzing-PCB-v1.ino
#include <Bridge.h>
#include <HttpClient.h>

char DEVID1[] = "v5AD1C1EB2754169"; //Scenario : "Shave-Butter-Device"
boolean DEBUG = true;
char serverName[] = "api.pushingbox.com";
int capWeight = A0;

void setup(){
  Serial.begin(9600);
  while (!Serial);
  Bridge.begin();
}

void loop(){
  int capWeight = analogRead(capWeight); 
  Serial.println(capWeight);

  if (capWeight >= 140 && capWeight <= 200) { 
   delay(1250);
    if (capWeight >= 140 && capWeight <= 200) {
      sendToPushingBox(DEVID1);
    }
    else {
      return;
    }
  } 
  delay(250);
}


void sendToPushingBox(char devid[])
{
  String APIRequest;
  
  Serial.println("Connecting to PushingBox ...");
  HttpClient client; 
  Serial.println("connected");
  Serial.println("sending request");
  
  //build API request
  APIRequest = String(serverName) + "/pushingbox?devid=" + String(devid);
  
  client.get (APIRequest);
    //DEBUG part
    // This write the response from PushingBox Server.
    // You should see a "200 OK"
    if (client.available()) 
    {
      char c = client.read();
      if(DEBUG){Serial.print(c);}
    }  
}
