# Fritzing sketch SB-Cap-Fritzing-PCB-v3-Particle+Lithium-Ion-SMD (saved by Fritzing 0.9.2b)
circuit board: 3.88975cm x 2.07472cm
breadboards: 1

parts:
  PR = Basic Force Sensing Resistor (FSR) [package=THT]
  TILT = Tilt Switch [package=THT]
  Photon_Sheild1 = Photon
  Part1 = Power Cell LiPo Charger/Booster
  R2 = Resistor [tolerance=±5% resistance=1k package="0805 [SMD]"]
  R1 = Resistor [tolerance=±5% resistance=1k package="0805 [SMD]"]

nets:
  N1: PR.pin_0, Photon_Sheild1.A0, R1.Pin_0
  GND: PR.pin_1, TILT.Pin_2, Photon_Sheild1.GND, Part1.GND
  N2: TILT.Pin_1, R2.Pin_1
  N3: Photon_Sheild1.VIN, Part1.5VIN, R2.Pin_0, R1.Pin_1

notes:
  Dollarshaveclub.com
  SB-Bomb-v2
